// Logisim project cpu.circ as structural Verilog: 1 circuit, main circuit cpu
module cpu (
  output [31:0] out_1,
  output out_2,
  output out_3,
  output [5:0] out_4,
  output out_5,
  output out_6,
  output out_7
);

  wire ALU_Src, Checker_out_2, Finish, mem_fetch_done, mem_mask_sel, not_1_out, not_2_out, not_3_out,
       not_4_out, not_5_out, Reg_Write, RegisterFile_p7, Zero;
  wire [1:0] mem_data_sel, MEMW_Sel, PC_control, Reg_Dest, Reg_Write_Sel, Shift_Select;
  wire [2:0] mem_addr_sel;
  wire [3:0] decoder_1_out0, multiplexer_8_out, multiplexer_10_out;
  wire [4:0] ALU_Ctrl, multiplexer_4_out, multiplexer_7_out;
  wire [5:0] Func;
  wire [7:0] miss_counter_state;
  wire [25:6] J_addr;
  wire [27:0] PC;
  wire [31:0] ALU_Result, cache_1_fetch0_addr, cache_1_fetch1_addr, cache_1_fetch2_addr, cache_1_fetch3_addr,
       cache_1_write_back0_addr, cache_1_write_back0_data, cache_1_write_back1_addr,
       cache_1_write_back1_data, cache_1_write_back2_addr, cache_1_write_back2_data,
       cache_1_write_back3_addr, cache_1_write_back3_data, Imm_ext, J_value, MemReadData, multiplexer_2_out,
       multiplexer_5_out, multiplexer_6_out, multiplexer_9_out, multiplexer_11_out, newPC, PC_4, PC_4_Imm,
       Read_Data1, Read_Data2, shifter_1_out;

  Clock clock_1 (.out(out_3));
  Shifter #(.width(32)) shifter_1 (.in(Imm_ext), .\dist (5'b00010), .out(shifter_1_out));
  Multiplexer multiplexer_1 (.in0(out_3), .in1(1'b0), .out(out_7), .sel(out_2));
  PLA #(.in_width(6), .out_width(1), .\table ("100011 1 # LW\n100000 1 # LB")) Checker (
    .in(out_4), .out(Checker_out_2));
  not not_1 (not_1_out, Finish);
  not not_2 (not_2_out, out_7);
  Adder #(.width(32)) adder_1 (.a({J_value[31:28], PC}), .b(32'h4), .out(PC_4));  // open: cin, cout
  Adder #(.width(32)) adder_2 (.a(PC_4), .b(shifter_1_out), .out(PC_4_Imm));  // open: cin, cout
  Shifter #(.width(28)) shifter_2 (.in({2'b00, J_addr, Func}), .\dist (5'b00010), .out(J_value[27:0]));
  Register #(.width(32)) u_PC (.D(newPC), .en(not_1_out), .clk(not_2_out), .Q({J_value[31:28], PC}));  // open: clr
  and and_1 (out_2, Checker_out_2, out_5);
  not not_3 (not_3_out, out_7);
  Multiplexer #(.width(32)) multiplexer_2 (.in0(PC_4_Imm), .in1(PC_4), .out(multiplexer_2_out), .sel(Zero));
  Multiplexer #(.select(2), .width(32)) multiplexer_3 (
    .in0(PC_4), .in1(multiplexer_2_out), .in2(J_value), .in3(Read_Data1), .out(newPC), .sel(PC_control));
  mem InstMem (
    .MemAddress({J_value[31:28], PC}), .MemWriteMask(4'b0000), .MemWriteData({32{1'b1}}), .clk(not_3_out),
    .MemReadData({out_4, J_addr, Func}));
  assign Imm_ext = {{16{J_addr[15]}}, {J_addr[15:6], Func}};  // Bit_Extender bit_extender_1
  // control_unit CU: pin names not known; wires that end beside it: out_4, Func, Reg_Write, ALU_Src, PC_control, Reg_Dest, Reg_Write_Sel, MEMW_Sel, Finish
  Multiplexer #(.select(2), .width(5)) multiplexer_4 (
    .in0(J_addr[20:16]), .in1(J_addr[15:11]), .in2({5{1'b1}}), .in3(5'b00001), .out(multiplexer_4_out),
    .sel(Reg_Dest));
  Multiplexer #(.select(2), .width(32)) multiplexer_5 (
    .in0(ALU_Result), .in1(MemReadData), .in2({J_value[31:28], PC}), .in3({{24{1'b0}}, MemReadData[7:0]}),
    .out(multiplexer_5_out), .sel(Reg_Write_Sel));
  Multiplexer #(.width(32)) multiplexer_6 (.in0(Read_Data2), .in1(Imm_ext), .out(multiplexer_6_out), .sel(ALU_Src));
  Decoder #(.enable("false"), .select(2)) decoder_1 (
    .out0(decoder_1_out0[0]), .out1(decoder_1_out0[1]), .out2(decoder_1_out0[2]), .out3(decoder_1_out0[3]),
    .sel(ALU_Result[1:0]));
  Multiplexer #(.select(2), .width(5)) multiplexer_7 (
    .in0(J_addr[10:6]), .in1(Read_Data1[4:0]), .in2(5'b10000), .in3({5{1'b0}}), .out(multiplexer_7_out),
    .sel(Shift_Select));
  // regfile RegisterFile: pin names not known; wires that end beside it: J_addr[25:21], J_addr[20:16], multiplexer_4_out, multiplexer_5_out, Reg_Write, out_7, RegisterFile_p7, Read_Data1, Read_Data2
  PLA #(.in_width(8), .out_width(7), .\table ("00000000 0000000 # w0_wb_addr\n00000001 0010001 # w1_wb_addr\n00000010 0100010 # w2 wb_addr\n00000011 0110011 # w3_wb_addr\n00000100 0001100 # w0_fetch_addr\n00000101 0001101 # w1_fetch_addr\n00000110 0001110 # w2_fetch_addr\n00000111 0001010 # w3_fetch_addr\n00001100 1000000 # mem_done")) pla_1 (
    .in(miss_counter_state), .out({mem_fetch_done, mem_data_sel, mem_mask_sel, mem_addr_sel}));
  Multiplexer #(.select(2), .width(4)) multiplexer_8 (
    .in0(4'b0000), .in1(4'b1111), .in2(decoder_1_out0), .in3(4'b0000), .out(multiplexer_8_out), .sel(MEMW_Sel));
  not not_4 (not_4_out, out_3);
  Counter #(.max('hc)) counter_1 (
    .clr(out_5), .load(1'b0), .up(1'b1), .clk(out_3), .Q(miss_counter_state));  // open: count, D, carry
  ALU ArithLogicUnit (
    .Input1(Read_Data1), .Input2(multiplexer_6_out), .op(ALU_Ctrl), .SHA(multiplexer_7_out), .Zero(Zero),
    .Result(ALU_Result));
  Cache cache_1 (
    .memWriteData(Read_Data2), .memAddress(ALU_Result), .clk(not_4_out), .write_mask(multiplexer_8_out),
    .miss_counter_state(miss_counter_state), .main_mem_read_data(out_1), .hit(out_5),
    .cacheReadData(MemReadData), .write_back0_addr(cache_1_write_back0_addr),
    .write_back1_addr(cache_1_write_back1_addr), .write_back2_addr(cache_1_write_back2_addr),
    .write_back3_addr(cache_1_write_back3_addr), .fetch0_addr(cache_1_fetch0_addr),
    .fetch1_addr(cache_1_fetch1_addr), .fetch2_addr(cache_1_fetch2_addr), .fetch3_addr(cache_1_fetch3_addr),
    .write_back0_data(cache_1_write_back0_data), .write_back2_data(cache_1_write_back2_data),
    .write_back1_data(cache_1_write_back1_data), .write_back3_data(cache_1_write_back3_data));
  // alu_control_unit ALU_Control: pin names not known; wires that end beside it: Func, out_4, ALU_Ctrl, Shift_Select
  not not_5 (not_5_out, out_5);
  Multiplexer #(.select(3), .width(32)) multiplexer_9 (
    .in0(cache_1_write_back0_addr), .in1(cache_1_write_back1_addr), .in2(cache_1_write_back2_addr),
    .in3(cache_1_write_back3_addr), .in4(cache_1_fetch0_addr), .in5(cache_1_fetch1_addr),
    .in6(cache_1_fetch2_addr), .in7(cache_1_fetch3_addr), .out(multiplexer_9_out), .sel(mem_addr_sel));
  Multiplexer #(.width(4)) multiplexer_10 (.in0(4'b1111), .in1(4'b0000), .out(multiplexer_10_out), .sel(mem_mask_sel));
  Multiplexer #(.select(2), .width(32)) multiplexer_11 (
    .in0(cache_1_write_back0_data), .in1(cache_1_write_back2_data), .in2(cache_1_write_back1_data),
    .in3(cache_1_write_back3_data), .out(multiplexer_11_out), .sel(mem_data_sel));
  and and_2 (out_6, out_3, not_5_out);
  memDelayed memdelayed_1 (
    .MemAddress(multiplexer_9_out), .MemWriteMask(multiplexer_10_out), .MemWriteData(multiplexer_11_out),
    .clk(out_6), .MemReadData(out_1));

  // Other names for the same wires on the sheet: J_addr[5:0] = Func; SHA[4:0] = J_addr[10:6]; rd[4:0] = J_addr[15:11];
  //   rt[4:0] = J_addr[20:16]; rs[4:0] = J_addr[25:21]; opcode[5:0] = out_4; Checker_Out = out_2; hit = out_5;
  //   PC[31:28] = J_value[31:28]; Main_Clock = out_3; main_mem_read_data[31:0] = out_1; reading_from_mem = out_6;
  //   Secondary_Clock = out_7

  // Notes on the sheet:
  //   PC Logic
  //   Clock
  //   Clk_Check
  //   Test_Outs
  //   Next
  //   Branch
  //   Jump
  //   JR
  //   Cache-memory
endmodule
